# Fritzing sketch Fingerprint Attendance (saved by Fritzing 0.9.3b)

parts:
  U1 = ESP32S-HiLetgo [part_number=ESP32S-HiLetgo]
  J1 = Piezo Speaker
  DFRobot_DFPlayer_Mini1 = DFRobot DFPlayer Mini [part_number=DFR0299]
  Part1 = sensor_biometrico
  SP1 = SPEAKER [package=pcb_mount_speaker]
  JACK_12V_DC = 2.1mm Barrel Jack with Terminal Block
  KY-1 = Keyes Relay [package=THT]
  Part2 = LCD1602-I2C
  SELENOID_DOOR_LOCK_12V = DC Motor

nets:
  N1: U1.GPIO14, J1.pin2
  GND: U1.GND, Part1.GND
  VIN: U1.VIN, Part1.VCC
  N2: U1.GPIO2, DFRobot_DFPlayer_Mini1.RX
  N3: U1.GPIO4, DFRobot_DFPlayer_Mini1.TX
  N4: U1.GPIO16, Part1.TX
  N5: U1.GPIO17, Part1.RX
  N6: U1.GPIO18, KY-1.ground
  N7: U1.GPIO21, Part2.SDA
  N8: U1.GPIO22, Part2.SCL
  N9: DFRobot_DFPlayer_Mini1.SPK_1, SP1.-
  N10: DFRobot_DFPlayer_Mini1.SPK_2, SP1.+
  N11: JACK_12V_DC.POS, SELENOID_DOOR_LOCK_12V.pin_2
  N12: JACK_12V_DC.NEG, KY-1.NO
  N13: KY-1.C, SELENOID_DOOR_LOCK_12V.pin_1

notes:
  SELENOID DOOR LOCK
  12V
  ADAPTOR 12V DC

custom parts:
  ESP32S-HiLetgo: HiLetgo ESP-WROOM-32 ESP32 ESP-32S Development Board 2.4GHz Dual-Mode WiFi + Bluetooth Dual Cores Microcontroller The ESP32 integrated with Antenna switches, RF Balun, power amplifiers, low-noise amplifiers, filters, and management modules, and the entire solution occupies the least area of PCB. 2.4 GHz Wi-Fi plus Bluetooth dual-mode chip, with TSMC Ultra-low power consumption 40nm technology,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
  sensor_biometrico: Adafruit Optical Fingerprint Sensor
  Keyes Relay: The Keyes 5V relay module is suitable for SCM development, home appliance control. It uses a 5V~12V TIL control signal which can control DC / AC signal.
  LCD1602-I2C: A standard character display, usually with 2x16 characters. Comes in many colors with LCM1602 IIC attached.
